# Fritzing sketch CellarWarden (saved by Fritzing 0.9.1b)
circuit board: 8.46667cm x 5.64444cm
breadboards: 1

parts:
  J1 = Cobbler Plus
  DHT1 = DHT22 Humidity and Temperature Sensor
  S1 = SPST Switch [package=switch-spdt]
  DHT2 = DHT22 Humidity and Temperature Sensor
  DS1 = DS18B20 1-Wire Temperature Sensor Probe Cable
  DS2 = DS18B20 1-Wire Temperature Sensor Probe Cable
  R1 = Resistor [tolerance=±5% resistance=4.7k package=THT]
  LCD1 = LCD screen
  R2 = Resistor [tolerance=±5% resistance=4.7k package=THT]
  R3 = Resistor [tolerance=±5% resistance=4.7k package=THT]
  U1 = TLP621 [package=THT]
  R4 = Resistor [tolerance=±5% resistance=470 package=THT]
  R5 = Resistor [tolerance=±5% resistance=330 package=THT]
  R6 = TRIMPOT [package=3386u]

nets (from the breadboard view):
  VDD: J1.3V3, DHT1.VDD, DHT2.VDD, DS1.VDD, DS2.VDD, R1.Pin_1, LCD1.VDD, R2.Pin_1, R3.Pin_1, U1.Pin_4, R6.CCW
  N1: J1.5.0V#3, DS1.shield, DS2.shield, R1.Pin_0
  N2: J1.#4, LCD1.E
  N3: J1.TXD, LCD1.RS
  N4: J1.#22, DHT1.DATA, R2.Pin_0
  N5: J1.#23, DHT2.DATA, R3.Pin_0
  N6: J1.MISO, S1.P
  GND: J1.SCLK, DHT1.GND, DHT2.GND, DS1.GND, DS2.GND, LCD1.VSS, LCD1.R/W, LCD1.LED-, R4.Pin_0, R6.CW
  N7: J1.CE1, LCD1.DB4
  N8: J1.EEC, LCD1.DB5
  N9: J1.#5, LCD1.DB6
  N10: J1.#6, LCD1.DB7
  N11: J1.#21, U1.Pin_3
  N12: S1.O, R5.Pin_0
  N13: S1.S, U1.Pin_1
  N14: LCD1.V0, R6.WIPER
  N15: LCD1.LED+, R5.Pin_1
  N16: U1.Pin_2, R4.Pin_1

custom parts:
  Cobbler Plus: The Cobbler Plus is an add on prototyping board from Adafruit specifically designed for the Raspberry Pi B+ that can break out all those tasty power, GPIO, I2C and SPI pins from the 40-pin header onto a solderless breadboard. This set will make "cobbling together" prototypes with the Pi super easy. The Cobbler Plus can plug into any solderless breadboard.
