# Fritzing sketch CellarWardenIO (saved by Fritzing 0.9.2b)
circuit board: 8.46667cm x 5.64444cm
breadboards: 1

parts:
  J1 = Cobbler Plus
  DHT1 = DHT22 Humidity and Temperature Sensor
  DS2 = DS18B20 1-Wire Temperature Sensor Probe Cable
  R1 = Resistor [tolerance=±5% resistance=4.7k package=THT]
  RTC1 = DS1307 RTC Breakout
  BB1 = 4-Line Bi-Directional Level Shifter
  BB2 = 4-Line Bi-Directional Level Shifter
  BB3 = 4-Line Bi-Directional Level Shifter
  R2 = Resistor [tolerance=±5% resistance=4.7k package=THT]
  DS3 = DS18B20 1-Wire Temperature Sensor Probe Cable
  R3 = Resistor [tolerance=±5% resistance=4.7k package=THT]
  DHT2 = DHT22 Humidity and Temperature Sensor
  U1 = LCD-16X2 [package=lcd-8x2-kit]

nets:
  N1: J1.CE1, BB3.A2
  VDD: DHT1.VDD, DS2.VDD, R1.Pin_0, RTC1.5V, R2.Pin_0, DS3.VDD, R3.Pin_0, DHT2.VDD, U1.VDD
  N2: DHT1.DATA, R1.Pin_1
  GND: DHT1.GND, DS2.GND, RTC1.GND, DS3.GND, DHT2.GND, U1.VSS
  N3: DS2.shield, R2.Pin_1, DS3.shield
  N4: RTC1.SDA, U1.RS
  N5: RTC1.SCL, U1.E
  N6: BB1.LV, BB2.LV, BB3.LV
  GND_2: BB1.GND, BB2.GND, BB3.GND
  N7: R3.Pin_1, DHT2.DATA

notes:
  I2C bus
  (5V Buffered)
  GPIO I/O
  (5V Buffered)
  20 x 4 LCD w/
  I2C Backpack

custom parts:
  Cobbler Plus: The Cobbler Plus is an add on prototyping board from Adafruit specifically designed for the Raspberry Pi B+ that can break out all those tasty power, GPIO, I2C and SPI pins from the 40-pin header onto a solderless breadboard. This set will make "cobbling together" prototypes with the Pi super easy. The Cobbler Plus can plug into any solderless breadboard.
  DS1307 RTC Breakout: DS1307 Real-time Clock Breakout Board with Battery
  4-Line Bi-Directional Level Shifter: 4-Channel Bi-Directional Level Shifter
