# Fritzing sketch CellarWardenMin (saved by Fritzing 0.9.1b)
circuit board: 8.46667cm x 5.64444cm
breadboards: 1

parts:
  J1 = Cobbler Plus
  DHT1 = DHT22 Humidity and Temperature Sensor
  S1 = SPST Switch [package=switch-spdt]
  DS2 = DS18B20 1-Wire Temperature Sensor Probe Cable
  R1 = Resistor [tolerance=±5% resistance=4.7k package=THT]
  R2 = Resistor [tolerance=±5% resistance=4.7k package=THT]

nets (from the breadboard view):
  VDD: J1.3V3, DHT1.VDD, S1.P, DS2.VDD, R1.Pin_1, R2.Pin_1
  N1: J1.5.0V#3, DS2.shield, R1.Pin_0
  GND: J1.SCL, DHT1.GND, DS2.GND
  N2: J1.#22, DHT1.DATA, R2.Pin_0
  N3: J1.#21, S1.S

custom parts:
  Cobbler Plus: The Cobbler Plus is an add on prototyping board from Adafruit specifically designed for the Raspberry Pi B+ that can break out all those tasty power, GPIO, I2C and SPI pins from the 40-pin header onto a solderless breadboard. This set will make "cobbling together" prototypes with the Pi super easy. The Cobbler Plus can plug into any solderless breadboard.
